# Fritzing sketch full_controller_setup (saved by Fritzing 0.9.3b)
breadboards: 1

parts:
  Part1 = Arduino Uno (Rev3)
  LD1 = LD
  LD2 = LD
  LD4 = LD
  LD3 = LD
  R3 = PHOTOCELL [package=photocell]
  R1 = PHOTOCELL [package=photocell]
  R4 = PHOTOCELL [package=photocell]
  R2 = PHOTOCELL [package=photocell]
  J1 = Piezo Speaker
  J2 = Piezo Speaker
  R9 = Resistor [tolerance=±5% resistance=1M package="2512 [SMD]"]
  R10 = Resistor [tolerance=±5% resistance=1M package="2512 [SMD]"]
  Part2 = Logic Level Converter
  Part3 = Logic Level Converter
  Part4 = 9-DOF Absolute Orientation IMU Fusion Breakout - BNO055
  Teensy_3_2 = Teensy 3.1
  S1 = Round Pushbutton

nets:
  N1: Part1.A0, R1.P$2
  N2: Part1.A1, R2.P$2
  N3: Part1.A2, R3.P$2
  N4: Part1.A3, R4.P$2
  N5: Part1.A4/SDA, R9.Pin_1
  N6: Part1.A5/SCL, R10.Pin_1
  GND: Part1.GND, LD1.cathode, LD2.cathode, LD4.cathode, LD3.cathode, R3.P$1, R1.P$1, R4.P$1, R2.P$1, J1.pin1, J2.pin1, Part2.GND, Part3.GND, Part4.GND, Teensy_3_2.GND
  N7: Part1.D0/RX, LD1.anode, LD2.anode, LD4.anode, LD3.anode
  N8: Part1.D1/TX, Part2.TX_HV
  N9: Part1.D2, Part2.RX_HV
  N10: Part1.D3_PWM, Part2.RX2_HV
  N11: Part1.D4, Part2.TX2_HV
  N12: Part1.D5_PWM, Part3.TX_HV
  N13: Part1.D6_PWM, Part3.RX_HV
  N14: Part1.3V3, Part2.LV, Part3.LV, S1.leg1
  N15: Part1.5V, Part2.HV, Part3.HV, Part4.5.0V
  N16: Part2.TX2_LV, Teensy_3_2.A8/D22
  N17: Part2.RX2_LV, Teensy_3_2.A3/D17
  N18: Part2.RX_LV, Teensy_3_2.D1
  N19: Part2.TX_LV, Teensy_3_2.D0
  N20: Part3.TX2_LV, Teensy_3_2.A4/D18
  N21: Part3.RX2_LV, Teensy_3_2.A5/D19
  N22: Part3.RX_LV, Teensy_3_2.D10
  N23: Part3.TX_LV, Teensy_3_2.D9
  N24: Part3.RX2_HV, Part4.SCL_5V
  N25: Part3.TX2_HV, Part4.SDA_5V
  N26: Teensy_3_2.A9/D23, S1.leg0

notes:
  Connections to OctoWS2811 Adapter Pins:
  Cyan -> 0
  Brown -> 1
  Orange -> 17
  Orange Banded -> 18
  Blue Banded -> 19
  Green -> 22
  Yellow -> 23
  Black -> GND
  Connections to Teensy Pins:
  Pink -> 9
  Blue -> 10
  Alternative (Requires soldering to bottom of board):
  Pink -> 18
  Blue -> 19
  Blue Banded -> 29
  Orange Banded -> 30
  Piezos
  Button
  BNO055
  Laser Gate

custom parts:
  LD: A Generic Red Dot Laser Diode Module (~5mW)
  9-DOF Absolute Orientation IMU Fusion Breakout - BNO055: A MEMS accelerometer, magnetometer and gyroscope on a single die with a high speed ARM Cortex-M0 based processor to digest all the sensor data, abstract the sensor fusion and real time requirements away, and spit out data you can use in quaternions, Euler angles or vectors.
