# Fritzing sketch laser_break_test (saved by Fritzing 0.9.3b)
breadboards: 1

parts:
  Part1 = Arduino Uno (Rev3)
  LD1 = LD
  LD2 = LD
  LD4 = LD
  LD3 = LD
  R5 = Resistor [tolerance=±5% resistance=10k package=THT]
  R3 = PHOTOCELL [package=photocell]
  R1 = PHOTOCELL [package=photocell]
  R4 = PHOTOCELL [package=photocell]
  R2 = PHOTOCELL [package=photocell]
  R6 = Resistor [tolerance=±5% resistance=10k package=THT]
  R7 = Resistor [tolerance=±5% resistance=10k package=THT]
  R8 = Resistor [tolerance=±5% resistance=220 package=THT]
  Part2 = ws2812b [package="smd 2812b"]
  S1 = Round Pushbutton

nets:
  N1: Part1.A0, R5.Pin_0, R4.P$2
  N2: Part1.A1, R3.P$2, R6.Pin_0
  N3: Part1.A2, R2.P$2, R7.Pin_0
  N4: Part1.A3, R1.P$2, R8.Pin_0
  GND: Part1.GND, LD1.cathode, LD2.cathode, LD4.cathode, LD3.cathode, R3.P$1, R1.P$1, R4.P$1, R2.P$1, Part2.VSS, S1.leg0
  N5: Part1.D2, S1.leg1
  N6: Part1.D3_PWM, LD1.anode, LD2.anode, LD4.anode, LD3.anode
  N7: Part1.D7, Part2.DIN
  5V: Part1.5V, R5.Pin_1, R7.Pin_1, R8.Pin_1, Part2.VDD

notes:
  Red = Const 5V
  Purple = Variable 5V
  Black= GND
  Everything else is for data

custom parts:
  LD: A Generic Red Dot Laser Diode Module (~5mW)
